# Fritzing sketch diagram (saved by Fritzing 0.9.3b)
breadboards: 1

parts:
  LCD1 = LCD screen
  Part1 = Arduino Uno (Rev3)
  U1 = 74HC595 [package="DIP16 [THT]"]
  Part2 = Thumb Joystick
  C1 = Electrolytic Capacitor [capacitance=1µF package="100 mil [THT, electrolytic]"]
  R1 = Trimmer Potentiometer [maximum_resistance=10kΩ package=THT]
  WeMos_D1_Mini_Relay_Shield_V1 = WeMos D1 Mini Relay Shield V2
  ZS-042_RTC1 = ZS-042 RTC Module
  DHT1 = DHT11_Temperature_and_Humitidy_Sensor
  Power_plug1 = Power plug
  R2 = Resistor [tolerance=±5% resistance=220 package=THT]  # not connected
  D3 = Rectifier Diode [part_number=1N4001 package="300 mil [THT]"]  # not connected
  VCC1 = Battery
  D2 = Rectifier Diode [part_number=1N4001 package="300 mil [THT]"]
  LED1 = LED - 5mm [color="Red (633nm)" package="5 mm [THT]"]
  LED2 = LED - 5mm [color="Red (633nm)" package="5 mm [THT]"]
  LED3 = LED - 5mm [color="Red (633nm)" package="5 mm [THT]"]
  LED4 = LED - 5mm [color="Red (633nm)" package="5 mm [THT]"]
  LED5 = LED - 5mm [color="Red (633nm)" package="5 mm [THT]"]
  LED6 = LED - 5mm [color="Red (633nm)" package="5 mm [THT]"]
  LED7 = LED - 5mm [color="Red (633nm)" package="5 mm [THT]"]
  LED8 = LED - 5mm [color="Red (633nm)" package="5 mm [THT]"]
  Part3 = Soil Moisture Sensor

nets:
  GND: LCD1.VSS, LCD1.R/W, LCD1.LED-, U1.GND, U1.OE, Part2.GND, C1.-, R1.leg2, WeMos_D1_Mini_Relay_Shield_V1.G, ZS-042_RTC1.GND, DHT1.connector4, Power_plug1.GND, VCC1.-, Part3.GND
  N1: LCD1.VDD, LCD1.LED+, R1.leg1, WeMos_D1_Mini_Relay_Shield_V1.COM
  N2: LCD1.V0, R1.wiper
  N3: LCD1.RS, Part1.D7
  N4: LCD1.E, Part1.D8
  N5: LCD1.DB4, Part1.D9_PWM
  N6: LCD1.DB5, Part1.D10_PWM/SS
  N7: LCD1.DB6, Part1.D11_PWM/MOSI
  N8: LCD1.DB7, Part1.D12/MISO
  N9: Part1.A0, Part2.HORZ
  N10: Part1.A1, Part2.VERT
  N11: Part1.A2, Part3.SIG
  N12: Part1.D13/SCK, DHT1.connector2
  N13: Part1.A4/SDA, ZS-042_RTC1.SDA
  N14: Part1.A5/SCL, ZS-042_RTC1.SCL
  N15: Part1.D2, Part2.SEL
  N16: Part1.D3_PWM, U1.SH_CP
  N17: Part1.D4, U1.ST_CP
  N18: Part1.D5_PWM, U1.DS
  N19: Part1.D6_PWM, WeMos_D1_Mini_Relay_Shield_V1.D1
  N20: U1.Q1, LED2.anode
  N21: U1.Q2, LED3.anode
  N22: U1.Q3, LED4.anode
  N23: U1.Q4, LED5.anode
  N24: U1.Q5, LED6.anode
  N25: U1.Q6, LED7.anode
  N26: U1.Q7, LED8.anode
  VCC: U1.MR, U1.VCC, Part2.VCC, WeMos_D1_Mini_Relay_Shield_V1.5V, WeMos_D1_Mini_Relay_Shield_V1.NC, ZS-042_RTC1.VCC, DHT1.connector1, D2.anode, Part3.VCC
  N27: U1.Q0, LED1.anode
  N28: Power_plug1.VCC, D2.cathode
